// Logisim project Mikroprozessor_A_8_v0.1.circ as structural Verilog: 1 circuit, main circuit main
module main (
);

  wire adder_1_cout, Ain, ALo, and_1_out, and_3_out, and_4_out, Bin, button_1_out, Cin, CLK, clock_1_out,
       Cot, Fin, HLT, JMC, JMP, JMZ, ldJ, ldS, Mot, nor_1_out, not_1_out, Oin, Oot, or_1_out, RAi, Rin, Rot,
       s_r_ff_1_q, seS, subtractor_1_bout;
  wire [3:0] register_7_q, register_7_q_2;
  wire [7:0] adder_1_out, controlled_buffer_3_out, controlled_buffer_5_out, ram_1_dout, register_1_q,
       register_2_q, register_3_q, register_4_q, register_5_q, register_6_q, register_8_q, register_9_q,
       rom_1_data, subtractor_1_out;
  wire [8:0] counter_1_q_2, undriven;
  wire [8:1] counter_1_q;
  wire [19:0] rom_2_data;
  wire [19:19] controlled_buffer_11_out;

  Button button_1 (.out(button_1_out));
  Counter #(.max('h1ff), .width(9)) counter_1 (
    .clr(button_1_out), .clk(CLK), .D(undriven), .Q({counter_1_q, counter_1_q_2[0]}));  // open: load, up, count, carry
  Register register_1 (.D(controlled_buffer_5_out), .en(ldJ), .clk(CLK), .Q(register_1_q));  // open: clr
  Register register_2 (.D(controlled_buffer_5_out), .en(Ain), .clk(CLK), .Q(register_2_q));  // open: clr
  Register register_3 (.D(controlled_buffer_5_out), .en(Bin), .clk(CLK), .Q(register_3_q));  // open: clr
  assign undriven[8:1] = or_1_out ? register_1_q : 8'bz;  // Controlled_Buffer controlled_buffer_1
  or or_1 (or_1_out, and_4_out, JMP, and_3_out);
  and and_1 (and_1_out, adder_1_cout, register_5_q[0]);
  and and_2 (and_1_out, subtractor_1_bout, register_5_q[1]);
  Register register_4 (.D(counter_1_q), .en(ldS), .clk(CLK), .Q(register_4_q));  // open: clr
  and and_3 (and_3_out, and_1_out, JMC);
  Register register_5 (.D(controlled_buffer_5_out), .en(Fin), .clk(CLK), .Q(register_5_q));  // open: clr
  Adder adder_1 (.a(register_2_q), .b(register_3_q), .out(adder_1_out), .cout(adder_1_cout));  // open: cin
  Subtractor subtractor_1 (
    .a(register_2_q), .b(register_3_q), .out(subtractor_1_out), .bout(subtractor_1_bout));  // open: bin
  assign undriven[8:1] = seS ? register_4_q : 8'bz;  // Controlled_Buffer controlled_buffer_2
  assign controlled_buffer_3_out = register_5_q[0] ? adder_1_out : 8'bz;  // Controlled_Buffer controlled_buffer_3
  assign controlled_buffer_3_out = register_5_q[1] ? subtractor_1_out : 8'bz;  // Controlled_Buffer controlled_buffer_4
  and and_4 (and_4_out, JMZ, nor_1_out);
  nor nor_1 (nor_1_out, register_6_q[7], register_6_q[6], register_6_q[5], register_6_q[4], register_6_q[3], register_6_q[2], register_6_q[1], register_6_q[0]);
  Register register_6 (.D(controlled_buffer_3_out), .en(1'b1), .clk(CLK), .Q(register_6_q));  // open: clr
  ROM #(.dataWidth(16)) rom_1 (.addr(counter_1_q), .data({counter_1_q_2[8:1], rom_1_data}));
  assign controlled_buffer_5_out = ALo ? register_6_q : 8'bz;  // Controlled_Buffer controlled_buffer_5
  Hex_Digit_Display hex_digit_display_1 (.value(register_7_q_2));  // open: dp
  Register register_7 (
    .D(controlled_buffer_5_out), .en(Oin), .clk(CLK), .Q({register_7_q_2, register_7_q}));  // open: clr
  Hex_Digit_Display hex_digit_display_2 (.value(register_7_q));  // open: dp
  assign controlled_buffer_5_out = Oot ? {register_7_q_2, register_7_q} : 8'bz;  // Controlled_Buffer controlled_buffer_6
  Register register_8 (.D(controlled_buffer_5_out), .en(RAi), .clk(CLK), .Q(register_8_q));  // open: clr
  RAM ram_1 (.addr(register_8_q), .we(Rin), .oe(1'b1), .clk(CLK), .din(controlled_buffer_5_out), .dout(ram_1_dout));
  assign controlled_buffer_5_out = Mot ? rom_1_data : 8'bz;  // Controlled_Buffer controlled_buffer_7
  Clock clock_1 (.out(clock_1_out));
  S_R_Flip_Flop s_r_ff_1 (.S(HLT), .clk(CLK), .Q(s_r_ff_1_q));  // open: R, reset, Qn, preset
  Register register_9 (.D(controlled_buffer_5_out), .en(Cin), .clk(CLK), .Q(register_9_q));  // open: clr
  assign CLK = not_1_out ? clock_1_out : 1'bz;  // Controlled_Buffer controlled_buffer_8
  not not_1 (not_1_out, s_r_ff_1_q);
  ROM #(.addrWidth(9), .dataWidth(20)) rom_2 (.addr(counter_1_q_2), .data(rom_2_data));
  assign controlled_buffer_5_out = Cot ? register_9_q : 8'bz;  // Controlled_Buffer controlled_buffer_9
  assign controlled_buffer_5_out = Rot ? ram_1_dout : 8'bz;  // Controlled_Buffer controlled_buffer_10
  assign {controlled_buffer_11_out[19], Oot, Oin, JMZ, JMC, JMP, ldJ, seS, ldS, ALo, Fin, Rot, Rin, RAi, Mot, Cot, Cin, Bin, Ain, HLT} = CLK ? rom_2_data : 20'bz;  // Controlled_Buffer controlled_buffer_11

  // Notes on the sheet:
  //   contents of rom_1 (hex, n*v repeats v):
  //   5ff 400 d00 c00
  //   contents of rom_2 (hex, n*v repeats v):
  //   60 102 60 104 60 108 60 90 28 0 60 480 60 300 10000 8000 4000 0 1 0 60 20100 60 40080
endmodule
